// Logisim project counter.circ as structural Verilog: 3 circuits, main circuit main
module main (
);

  wire and_1_out, and_2_out, and_3_out, and_4_out, and_5_out, button_1_out, counter_1_q0, counter_1_q1,
       counter_1_q2, counter_1_q3, counter_2_q0, counter_2_q1, counter_2_q2, counter_2_q3, counter_3_q0,
       counter_3_q1, counter_3_q2, counter_3_q3, counter_4_q0, counter_4_q1, counter_4_q2, counter_4_q3,
       counter_5_q0, counter_5_q1, counter_5_q2, counter_5_q3, n7segmenteddisplaydecoder_1_a,
       n7segmenteddisplaydecoder_1_b, n7segmenteddisplaydecoder_1_c, n7segmenteddisplaydecoder_1_d,
       n7segmenteddisplaydecoder_1_e, n7segmenteddisplaydecoder_1_f, n7segmenteddisplaydecoder_1_g,
       n7segmenteddisplaydecoder_2_a, n7segmenteddisplaydecoder_2_b, n7segmenteddisplaydecoder_2_c,
       n7segmenteddisplaydecoder_2_d, n7segmenteddisplaydecoder_2_e, n7segmenteddisplaydecoder_2_f,
       n7segmenteddisplaydecoder_2_g, n7segmenteddisplaydecoder_3_a, n7segmenteddisplaydecoder_3_b,
       n7segmenteddisplaydecoder_3_c, n7segmenteddisplaydecoder_3_d, n7segmenteddisplaydecoder_3_e,
       n7segmenteddisplaydecoder_3_f, n7segmenteddisplaydecoder_3_g, n7segmenteddisplaydecoder_4_a,
       n7segmenteddisplaydecoder_4_b, n7segmenteddisplaydecoder_4_c, n7segmenteddisplaydecoder_4_d,
       n7segmenteddisplaydecoder_4_e, n7segmenteddisplaydecoder_4_f, n7segmenteddisplaydecoder_4_g,
       n7segmenteddisplaydecoder_5_a, n7segmenteddisplaydecoder_5_b, n7segmenteddisplaydecoder_5_c,
       n7segmenteddisplaydecoder_5_d, n7segmenteddisplaydecoder_5_e, n7segmenteddisplaydecoder_5_f,
       n7segmenteddisplaydecoder_5_g, or_1_out, or_2_out, or_3_out, or_4_out, or_5_out, R_out;

  _7_Segment_Display u_7_segment_display_1 (
    .g(n7segmenteddisplaydecoder_1_d), .f(n7segmenteddisplaydecoder_1_e), .a(n7segmenteddisplaydecoder_1_f),
    .b(n7segmenteddisplaydecoder_1_g), .e(n7segmenteddisplaydecoder_1_a), .d(n7segmenteddisplaydecoder_1_b),
    .c(n7segmenteddisplaydecoder_1_c));  // open: dp
  _7SegmentedDisplayDecoder u_7segmenteddisplaydecoder_1 (
    .I4(counter_1_q3), .I3(counter_1_q2), .I2(counter_1_q1), .I1(counter_1_q0),
    .a(n7segmenteddisplaydecoder_1_a), .b(n7segmenteddisplaydecoder_1_b), .c(n7segmenteddisplaydecoder_1_c),
    .d(n7segmenteddisplaydecoder_1_d), .e(n7segmenteddisplaydecoder_1_e), .f(n7segmenteddisplaydecoder_1_f),
    .g(n7segmenteddisplaydecoder_1_g));
  and and_1 (and_1_out, counter_1_q3, counter_1_q1);
  or or_1 (or_1_out, R_out, and_1_out);
  Counter counter_1 (
    .Clock(or_2_out), .Reset(or_1_out), .Q3(counter_1_q3), .Q2(counter_1_q2), .Q1(counter_1_q1),
    .Q0(counter_1_q0));
  and and_2 (and_2_out, counter_2_q3, counter_2_q1);
  or or_2 (or_2_out, R_out, and_2_out);
  _7_Segment_Display u_7_segment_display_2 (
    .g(n7segmenteddisplaydecoder_2_d), .f(n7segmenteddisplaydecoder_2_e), .a(n7segmenteddisplaydecoder_2_f),
    .b(n7segmenteddisplaydecoder_2_g), .e(n7segmenteddisplaydecoder_2_a), .d(n7segmenteddisplaydecoder_2_b),
    .c(n7segmenteddisplaydecoder_2_c));  // open: dp
  _7SegmentedDisplayDecoder u_7segmenteddisplaydecoder_2 (
    .I4(counter_2_q3), .I3(counter_2_q2), .I2(counter_2_q1), .I1(counter_2_q0),
    .a(n7segmenteddisplaydecoder_2_a), .b(n7segmenteddisplaydecoder_2_b), .c(n7segmenteddisplaydecoder_2_c),
    .d(n7segmenteddisplaydecoder_2_d), .e(n7segmenteddisplaydecoder_2_e), .f(n7segmenteddisplaydecoder_2_f),
    .g(n7segmenteddisplaydecoder_2_g));
  Counter counter_2 (
    .Clock(or_3_out), .Reset(or_2_out), .Q3(counter_2_q3), .Q2(counter_2_q2), .Q1(counter_2_q1),
    .Q0(counter_2_q0));
  _7_Segment_Display u_7_segment_display_3 (
    .g(n7segmenteddisplaydecoder_3_d), .f(n7segmenteddisplaydecoder_3_e), .a(n7segmenteddisplaydecoder_3_f),
    .b(n7segmenteddisplaydecoder_3_g), .e(n7segmenteddisplaydecoder_3_a), .d(n7segmenteddisplaydecoder_3_b),
    .c(n7segmenteddisplaydecoder_3_c));  // open: dp
  _7SegmentedDisplayDecoder u_7segmenteddisplaydecoder_3 (
    .I4(counter_3_q3), .I3(counter_3_q2), .I2(counter_3_q1), .I1(counter_3_q0),
    .a(n7segmenteddisplaydecoder_3_a), .b(n7segmenteddisplaydecoder_3_b), .c(n7segmenteddisplaydecoder_3_c),
    .d(n7segmenteddisplaydecoder_3_d), .e(n7segmenteddisplaydecoder_3_e), .f(n7segmenteddisplaydecoder_3_f),
    .g(n7segmenteddisplaydecoder_3_g));
  and and_3 (and_3_out, counter_3_q3, counter_3_q1);
  Counter counter_3 (
    .Clock(or_4_out), .Reset(or_3_out), .Q3(counter_3_q3), .Q2(counter_3_q2), .Q1(counter_3_q1),
    .Q0(counter_3_q0));
  or or_3 (or_3_out, and_3_out, R_out);
  _7_Segment_Display u_7_segment_display_4 (
    .g(n7segmenteddisplaydecoder_4_d), .f(n7segmenteddisplaydecoder_4_e), .a(n7segmenteddisplaydecoder_4_f),
    .b(n7segmenteddisplaydecoder_4_g), .e(n7segmenteddisplaydecoder_4_a), .d(n7segmenteddisplaydecoder_4_b),
    .c(n7segmenteddisplaydecoder_4_c));  // open: dp
  _7SegmentedDisplayDecoder u_7segmenteddisplaydecoder_4 (
    .I4(counter_4_q3), .I3(counter_4_q2), .I2(counter_4_q1), .I1(counter_4_q0),
    .a(n7segmenteddisplaydecoder_4_a), .b(n7segmenteddisplaydecoder_4_b), .c(n7segmenteddisplaydecoder_4_c),
    .d(n7segmenteddisplaydecoder_4_d), .e(n7segmenteddisplaydecoder_4_e), .f(n7segmenteddisplaydecoder_4_f),
    .g(n7segmenteddisplaydecoder_4_g));
  and and_4 (and_4_out, counter_4_q3, counter_4_q1);
  Counter counter_4 (
    .Clock(or_5_out), .Reset(or_4_out), .Q3(counter_4_q3), .Q2(counter_4_q2), .Q1(counter_4_q1),
    .Q0(counter_4_q0));
  or or_4 (or_4_out, R_out, and_4_out);
  and and_5 (and_5_out, counter_5_q3, counter_5_q1);
  or or_5 (or_5_out, R_out, and_5_out);
  Button R (.out(R_out));
  _7_Segment_Display u_7_segment_display_5 (
    .g(n7segmenteddisplaydecoder_5_d), .f(n7segmenteddisplaydecoder_5_e), .a(n7segmenteddisplaydecoder_5_f),
    .b(n7segmenteddisplaydecoder_5_g), .e(n7segmenteddisplaydecoder_5_a), .d(n7segmenteddisplaydecoder_5_b),
    .c(n7segmenteddisplaydecoder_5_c));  // open: dp
  _7SegmentedDisplayDecoder u_7segmenteddisplaydecoder_5 (
    .I4(counter_5_q3), .I3(counter_5_q2), .I2(counter_5_q1), .I1(counter_5_q0),
    .a(n7segmenteddisplaydecoder_5_a), .b(n7segmenteddisplaydecoder_5_b), .c(n7segmenteddisplaydecoder_5_c),
    .d(n7segmenteddisplaydecoder_5_d), .e(n7segmenteddisplaydecoder_5_e), .f(n7segmenteddisplaydecoder_5_f),
    .g(n7segmenteddisplaydecoder_5_g));
  Counter counter_5 (
    .Clock(button_1_out), .Reset(or_5_out), .Q3(counter_5_q3), .Q2(counter_5_q2), .Q1(counter_5_q1),
    .Q0(counter_5_q0));
  Button button_1 (.out(button_1_out));

  // Notes on the sheet:
  //   Reset
  //   Counter
endmodule

module _7SegmentedDisplayDecoder (
  input  I4,
  input  I3,
  input  I2,
  input  I1,
  output a,
  output b,
  output c,
  output d,
  output e,
  output f,
  output g
);

  wire and_1_out, and_2_out, and_3_out, and_4_out, and_5_out, and_6_out, and_7_out, and_8_out, and_9_out,
       and_10_out, and_11_out, and_12_out, and_13_out, and_14_out, and_15_out, and_16_out, and_17_out,
       and_18_out, and_19_out, and_20_out, and_21_out, and_22_out, and_23_out, and_24_out, and_25_out,
       and_26_out, and_27_out, and_28_out, and_29_out, and_30_out, and_31_out, and_32_out, and_33_out,
       and_34_out, and_35_out, and_36_out, not_1_out, not_2_out, not_3_out, not_4_out, not_5_out, not_6_out,
       not_7_out, not_8_out, not_9_out, not_10_out, not_11_out, not_12_out, not_13_out, not_14_out,
       not_15_out, not_16_out, not_17_out, not_18_out, not_19_out, not_20_out, not_21_out, not_22_out,
       not_23_out, not_24_out, not_25_out, not_26_out, not_27_out, not_28_out, not_29_out, not_30_out,
       not_31_out, not_32_out, not_33_out, not_34_out, not_35_out, not_36_out, not_37_out, not_38_out,
       not_39_out, not_40_out, not_41_out, not_42_out, not_43_out, not_44_out, not_45_out;

  not not_1 (not_1_out, I3);
  and and_1 (and_1_out, not_1_out, not_2_out);
  not not_2 (not_2_out, I1);
  and and_2 (and_2_out, I2, not_3_out);
  not not_3 (not_3_out, I1);
  and and_3 (and_3_out, I4, I2);
  and and_4 (and_4_out, I4, I3);
  not not_4 (not_4_out, I3);
  and and_5 (and_5_out, not_4_out, not_5_out, not_6_out);
  not not_5 (not_5_out, I2);
  not not_6 (not_6_out, I1);
  not not_7 (not_7_out, I4);
  and and_6 (and_6_out, not_7_out, I2, not_8_out);
  not not_8 (not_8_out, I1);
  not not_9 (not_9_out, I3);
  and and_7 (and_7_out, not_9_out, I2, I1);
  not not_10 (not_10_out, I2);
  and and_8 (and_8_out, I3, not_10_out, I1);
  and and_9 (and_9_out, I4, I3, not_11_out);
  not not_11 (not_11_out, I1);
  not not_12 (not_12_out, I3);
  and and_10 (and_10_out, not_12_out, not_13_out);
  not not_13 (not_13_out, I2);
  not not_14 (not_14_out, I3);
  and and_11 (and_11_out, not_14_out, I1);
  not not_15 (not_15_out, I2);
  and and_12 (and_12_out, not_15_out, I1);
  not not_16 (not_16_out, I4);
  and and_13 (and_13_out, not_16_out, I3);
  and and_14 (and_14_out, I4, not_17_out);
  not not_17 (not_17_out, I3);
  not not_18 (not_18_out, I3);
  and and_15 (and_15_out, not_18_out, I2);
  and and_16 (and_16_out, I2, not_19_out);
  not not_19 (not_19_out, I1);
  not not_20 (not_20_out, I4);
  and and_17 (and_17_out, not_20_out, I3, not_21_out);
  not not_21 (not_21_out, I1);
  and and_18 (and_18_out, I3, not_22_out, I1);
  not not_22 (not_22_out, I2);
  and and_19 (and_19_out, I4, not_23_out);
  not not_23 (not_23_out, I3);
  and and_20 (and_20_out, I4, I2);
  not not_24 (not_24_out, I2);
  and and_21 (and_21_out, not_24_out, not_25_out);
  not not_25 (not_25_out, I1);
  not not_26 (not_26_out, I4);
  and and_22 (and_22_out, not_26_out, I3, not_27_out);
  not not_27 (not_27_out, I2);
  and and_23 (and_23_out, I3, not_28_out);
  not not_28 (not_28_out, I1);
  and and_24 (and_24_out, I4, not_29_out);
  not not_29 (not_29_out, I3);
  and and_25 (and_25_out, I4, I2);
  not not_30 (not_30_out, I3);
  and and_26 (and_26_out, not_30_out, not_31_out);
  not not_31 (not_31_out, I1);
  not not_32 (not_32_out, I4);
  and and_27 (and_27_out, not_32_out, I2, I1);
  not not_33 (not_33_out, I4);
  and and_28 (and_28_out, not_33_out, I3, I1);
  and and_29 (and_29_out, I3, I2, I1);
  and and_30 (and_30_out, I4, not_34_out, not_35_out);
  not not_34 (not_34_out, I3);
  not not_35 (not_35_out, I2);
  and and_31 (and_31_out, I4, not_36_out);
  not not_36 (not_36_out, I1);
  not not_37 (not_37_out, I4);
  not not_38 (not_38_out, I2);
  and and_32 (and_32_out, not_37_out, not_38_out, not_39_out);
  not not_39 (not_39_out, I1);
  not not_40 (not_40_out, I3);
  and and_33 (and_33_out, not_40_out, not_41_out);
  not not_41 (not_41_out, I2);
  not not_42 (not_42_out, I3);
  and and_34 (and_34_out, not_42_out, not_43_out);
  not not_43 (not_43_out, I1);
  not not_44 (not_44_out, I4);
  and and_35 (and_35_out, not_44_out, I2, I1);
  and and_36 (and_36_out, I4, not_45_out, I1);
  not not_45 (not_45_out, I2);
  or or_1 (a, and_1_out, and_2_out, and_3_out, and_4_out);
  or or_2 (b, and_5_out, and_6_out, and_7_out, and_8_out, and_9_out);
  or or_3 (c, and_10_out, and_11_out, and_12_out, and_13_out, and_14_out);
  or or_4 (e, and_21_out, and_22_out, and_23_out, and_24_out, and_25_out);
  or or_5 (g, and_32_out, and_33_out, and_34_out, and_35_out, and_36_out);
  or or_6 (d, and_15_out, and_16_out, and_17_out, and_18_out, and_19_out, and_20_out);
  or or_7 (f, and_26_out, and_27_out, and_28_out, and_29_out, and_30_out, and_31_out);
endmodule

module Counter (
  input  Clock,
  input  Reset,
  output Q3,
  output Q2,
  output Q1,
  output Q0
);

  wire t_ff_1_qn, t_ff_2_qn, t_ff_3_qn;

  T_Flip_Flop t_ff_1 (.clk(Clock), .T(1'b1), .Q(Q0), .Qn(t_ff_1_qn), .reset(Reset));  // open: preset, en
  T_Flip_Flop t_ff_2 (.clk(t_ff_1_qn), .T(1'b1), .Q(Q1), .Qn(t_ff_2_qn), .reset(Reset));  // open: preset, en
  T_Flip_Flop t_ff_3 (.clk(t_ff_2_qn), .T(1'b1), .Q(Q2), .Qn(t_ff_3_qn), .reset(Reset));  // open: preset, en
  T_Flip_Flop t_ff_4 (.clk(t_ff_3_qn), .T(1'b1), .Q(Q3), .reset(Reset));  // open: Qn, preset, en
endmodule
